# Fritzing sketch Caja Fuerte (saved by Fritzing 0.9.3b)
breadboards: 1

parts:
  Part1 = Arduino Uno (Rev3)
  LCD1 = LCD screen
  R1 = Rotary Potentiometer (Large) [maximum_resistance=100kΩ package=THT]

nets:
  5V: Part1.5V, LCD1.VDD, LCD1.LED+
  GND: Part1.GND, LCD1.VSS, LCD1.LED-, R1.leg1, R1.leg2
  N1: LCD1.V0, R1.wiper

// code stored in the sketch: Codigo.ino

